// Logisim project 2_lab_4.circ as structural Verilog: 1 circuit, main circuit main
module main (
  input  in_1,
  input  in_2,
  input  in_3,
  input  in_4,
  output B_prime,
  output D_prime,
  output A_prime
);

  wire and_1_out, and_2_out, and_3_out, and_4_out, and_5_out, and_6_out, and_7_out, and_8_out, and_9_out,
       not_2_out, not_3_out, not_4_out;

  not not_1 (D_prime, in_4);
  not not_2 (not_2_out, in_1);
  not not_3 (not_3_out, in_2);
  not not_4 (not_4_out, in_3);
  and and_1 (and_1_out, in_4, not_4_out);
  and and_2 (and_2_out, in_3, D_prime);
  // OR_Gate or_1 has open pins: in0=and_1_out, in1=and_2_out, out=open
  and and_3 (and_3_out, in_2, not_4_out);
  and and_4 (and_4_out, in_2, D_prime);
  and and_5 (and_5_out, not_3_out, in_4, in_3);
  and and_6 (and_6_out, not_2_out, not_4_out);
  and and_7 (and_7_out, not_2_out, D_prime);
  and and_8 (and_8_out, not_2_out, not_3_out);
  and and_9 (and_9_out, in_1, in_2, in_3, in_4);
  or or_2 (B_prime, and_3_out, and_4_out, and_5_out);
  or or_3 (A_prime, and_6_out, and_7_out, and_8_out, and_9_out);

  // Notes on the sheet:
  //   A
  //   !A
  //   !B
  //   !C
  //   !D
  //   !A
  //   B
  //   C
  //   D
  //   !B
  //   !C
  //   !D
  //   C`
endmodule
